// Logisim project Logisim_RISC.circ as structural Verilog: 9 circuits, main circuit common_bus
module control_unit_o (
  input  [15:0] IR_0_15,
  input  seq_clk,
  input  seq_inr,
  input  seq_clr,
  output [11:0] CU_B_output,
  output I_output,
  output D0,
  output D1,
  output D2,
  output D3,
  output D4,
  output D5,
  output D6,
  output D7,
  output [15:0] seq_output
);

  wire [3:0] seq_counter_o_1_t_0_15;

  Decoder #(.enable("false"), .select(3)) decoder_1 (
    .out0(D0), .out1(D1), .out2(D2), .out3(D3), .out4(D4), .out5(D5), .out6(D6), .out7(D7),
    .sel(IR_0_15[14:12]));
  Seq_Counter_o seq_counter_o_1 (
    .seq_clk(seq_clk), .seq_inr(seq_inr), .seq_clr(seq_clr), .T_0_15(seq_counter_o_1_t_0_15));
  Decoder #(.enable("false"), .select(4)) decoder_2 (
    .out0(seq_output[0]), .out1(seq_output[1]), .out2(seq_output[2]), .out3(seq_output[3]),
    .out4(seq_output[4]), .out5(seq_output[5]), .out6(seq_output[6]), .out7(seq_output[7]),
    .out8(seq_output[8]), .out9(seq_output[9]), .out10(seq_output[10]), .out11(seq_output[11]),
    .out12(seq_output[12]), .out13(seq_output[13]), .out14(seq_output[14]), .out15(seq_output[15]),
    .sel(seq_counter_o_1_t_0_15));

  assign CU_B_output = IR_0_15[11:0];
  assign I_output = IR_0_15[15];
endmodule

module Seq_Counter_o (
  input  seq_clk,
  input  seq_inr,
  input  seq_clr,
  output [3:0] T_0_15
);

  wire [3:0] adder_1_out, multiplexer_1_out, multiplexer_2_out;

  Adder #(.width(4)) adder_1 (.a(T_0_15), .b(4'b0001), .out(adder_1_out));  // open: cin, cout
  Multiplexer #(.width(4)) multiplexer_1 (.in0(T_0_15), .in1(adder_1_out), .out(multiplexer_1_out), .sel(seq_inr));
  Multiplexer #(.width(4)) multiplexer_2 (
    .in0(multiplexer_1_out), .in1(4'b0000), .out(multiplexer_2_out), .sel(seq_clr));
  Register #(.width(4)) register_1 (.D(multiplexer_2_out), .clk(seq_clk), .Q(T_0_15));  // open: en, clr

  // Other names for the same wires on the sheet: CLR = seq_clr; INR = seq_inr
endmodule

module common_bus (
  input  Write,
  input  en,
  input  Clk,
  input  Incr_ar,
  input  Load_ar,
  input  Clr_ar,
  input  Incr_pc,
  input  Load_pc,
  input  [2:0] S2S1S0,
  input  Clr_pc,
  input  Incr_dr,
  input  Load_dr,
  input  Clr_dr,
  input  Incr_accu,
  input  load_ac,
  input  Clr_accu,
  input  [2:0] ALUselect,
  input  Incr_ir,
  input  Load_ir,
  input  Clr_ir,
  input  Incr_tr,
  input  Load_tr,
  input  Clr_tr,
  input  ComE,
  input  Load,
  input  Clr,
  output [15:0] ar_0_15,
  output [11:0] pc_output,
  output [15:0] dr_0_15,
  output [15:0] ac_0_15,
  output [15:0] ir_0_15,
  output E_ff_op
);

  wire Cout, E_FF_op_t;
  wire [15:0] arithmeticlogicalunit_1_aluout, multiplexer_1_out, ram_1_dout, TR_outpin;

  // Probe on multiplexer_1_out
  ArithmeticLogicalUnit arithmeticlogicalunit_1 (
    .AC(ac_0_15), .DR(dr_0_15), .IPLS(E_FF_op_t), .IPRS(E_FF_op_t), .ALUselect(ALUselect),
    .ALUout(arithmeticlogicalunit_1_aluout), .Cout(Cout));
  // Probe on arithmeticlogicalunit_1_aluout
  E_ff e_ff_1 (.comE(ComE), .E_ip(Cout), .load(Load), .clr(Clr), .clk(Clk), .E_ff_op(E_ff_op));
  RAM #(.addrWidth(12), .asyncread("true"), .dataWidth(16)) ram_1 (
    .addr(ar_0_15[11:0]), .we(Write), .oe(en), .clk(Clk), .din(multiplexer_1_out), .dout(ram_1_dout));
  register12bit AR (
    .INR(Incr_ar), .LD(Load_ar), .CLR(Clr_ar), .clk(Clk), .inpPin(multiplexer_1_out[11:0]),
    .outPin(ar_0_15[11:0]));
  register12bit PC (
    .INR(Incr_pc), .LD(Load_pc), .CLR(Clr_pc), .clk(Clk), .inpPin(multiplexer_1_out[11:0]), .outPin(pc_output));
  register16bit_exp DR (
    .INR(Incr_dr), .LD(Load_dr), .CLR(Clr_dr), .clk(Clk), .inpPin(multiplexer_1_out), .outPin(dr_0_15));
  register16bit_exp Accumulator (
    .INR(Incr_accu), .LD(load_ac), .CLR(Clr_accu), .clk(Clk), .inpPin(arithmeticlogicalunit_1_aluout),
    .outPin(ac_0_15));
  register16bit_exp IR (
    .INR(Incr_ir), .LD(Load_ir), .CLR(Clr_ir), .clk(Clk), .inpPin(multiplexer_1_out), .outPin(ir_0_15));
  register16bit_exp TR (
    .INR(Incr_tr), .LD(Load_tr), .CLR(Clr_tr), .clk(Clk), .inpPin(multiplexer_1_out), .outPin(TR_outpin));
  // Probe on ram_1_dout
  // Probe on {4'b0000, ar_0_15[11:0]}
  Multiplexer #(.select(3), .width(16)) multiplexer_1 (
    .in1({4'b0000, ar_0_15[11:0]}), .in2({4'b0000, pc_output}), .in3(dr_0_15), .in4(ac_0_15), .in5(ir_0_15),
    .in6(TR_outpin), .in7(ram_1_dout), .out(multiplexer_1_out), .sel(S2S1S0));  // open: in0
  // Probe on multiplexer_1_out

  assign ar_0_15[15:12] = 4'b0000;

  // Other names for the same wires on the sheet: address[11:0] = ar_0_15[11:0]; sclk = Clk
endmodule

module register16bit_exp (
  input  INR,
  input  LD,
  input  CLR,
  input  clk,
  input  [15:0] inpPin,
  output [15:0] outPin
);

  wire [15:0] adder_1_out, multiplexer_1_out, multiplexer_2_out, multiplexer_3_out;

  Adder #(.width(16)) adder_1 (.a(outPin), .b(16'h1), .out(adder_1_out), .cin(1'b0));  // open: cout
  Multiplexer #(.width(16)) multiplexer_1 (.in0(outPin), .in1(adder_1_out), .out(multiplexer_1_out), .sel(INR));
  Multiplexer #(.width(16)) multiplexer_2 (.in0(multiplexer_1_out), .in1(inpPin), .out(multiplexer_2_out), .sel(LD));
  Multiplexer #(.width(16)) multiplexer_3 (
    .in0(multiplexer_2_out), .in1({16{1'b0}}), .out(multiplexer_3_out), .sel(CLR));
  Register #(.width(16)) register_1 (.D(multiplexer_3_out), .clk(clk), .Q(outPin));  // open: en, clr
endmodule

module register12bit (
  input  INR,
  input  LD,
  input  CLR,
  input  clk,
  input  [11:0] inpPin,
  output [11:0] outPin
);

  wire [11:0] adder_1_out, multiplexer_1_out, multiplexer_2_out, multiplexer_3_out;

  Adder #(.width(12)) adder_1 (.a(outPin), .b(12'h1), .out(adder_1_out), .cin(1'b0));  // open: cout
  Multiplexer #(.width(12)) multiplexer_1 (.in0(outPin), .in1(adder_1_out), .out(multiplexer_1_out), .sel(INR));
  Multiplexer #(.width(12)) multiplexer_2 (.in0(multiplexer_1_out), .in1(inpPin), .out(multiplexer_2_out), .sel(LD));
  Multiplexer #(.width(12)) multiplexer_3 (
    .in0(multiplexer_2_out), .in1({12{1'b0}}), .out(multiplexer_3_out), .sel(CLR));
  Register #(.width(12)) register_1 (.D(multiplexer_3_out), .clk(clk), .Q(outPin));  // open: en, clr
endmodule

module E_ff (
  input  comE,
  input  E_ip,
  input  load,
  input  clr,
  input  clk,
  output E_ff_op
);

  wire multiplexer_1_out, multiplexer_2_out, multiplexer_3_out, not_1_out;

  not not_1 (not_1_out, E_ff_op);
  Multiplexer multiplexer_1 (.in0(E_ff_op), .in1(not_1_out), .out(multiplexer_1_out), .sel(comE));
  Multiplexer multiplexer_2 (.in0(multiplexer_1_out), .in1(E_ip), .out(multiplexer_2_out), .sel(load));
  Multiplexer multiplexer_3 (.in0(multiplexer_2_out), .in1(1'b0), .out(multiplexer_3_out), .sel(clr));
  D_Flip_Flop d_ff_1 (.D(multiplexer_3_out), .clk(clk), .Q(E_ff_op));  // open: Qn, preset, reset
endmodule

module main_circuit (
  input  in_1,
  input  in_2,
  output r,
  output rB11,
  output rB10,
  output rB9,
  output rB8,
  output rB7,
  output rB6,
  output rB5,
  output rB4,
  output rB3,
  output rB2,
  output rB1,
  output rB0,
  output out_16,
  output out_17,
  output out_18,
  output out_19,
  output out_20,
  output out_21
);

  wire a0, a1, a2, a3, a4, a5, ACEql0, and_1_out, and_2_out, and_3_out, and_4_out, and_6_out, and_7_out,
       and_8_out, and_9_out, and_10_out, and_11_out, and_14_out, and_16_out, and_17_out, and_18_out,
       and_19_out, and_20_out, and_21_out, and_22_out, and_23_out, and_24_out, and_25_out, and_40_out,
       and_41_out, and_42_out, and_43_out, and_44_out, and_45_out, and_46_out, and_47_out, and_48_out,
       and_49_out, and_50_out, and_51_out, B0, B1, B2, B3, B4, B5, B6, B7, B8, B9, B10, B11, Clk, CLR, D0,
       D1, D2, D3, D4, D5, D6, D7, DREqI0, E_COMP, E_ff_op, En_rd, I_output, INC_DR, INC_PC, LD_DR, LD_IR,
       LD_PC, LOAD, not_1_out, not_2_out, not_3_out, not_4_out, not_7_out, not_8_out, or_2_out, or_6_out,
       or_7_out, or_8_out, or_9_out, or_10_out, or_14_out, or_15_out, or_16_out, or_19_out, rdEN, S0, S1, S2,
       seq_inr, T0, T2, T3, T4, T5, T6, T7, T8, T9, T10, T11, T12, T13, T14, T15, W_En, X1, X2, X3, X4, X5, Y;
  wire [2:0] AL_S2S1S0;
  wire [11:0] common_bus_1_pc_output;
  wire [15:0] AC_0_15, common_bus_1_ar_0_15, common_bus_1_ir_0_15, DR_0_15;

  and and_1 (and_1_out, D6, T6);
  and and_2 (and_2_out, D3, T4);
  and and_3 (and_3_out, D5, T4);
  and and_4 (and_4_out, D6, T6);
  not not_1 (not_1_out, AC_0_15[15]);
  and and_5 (out_16, D5, T4);
  or or_1 (out_17, T0, T2, r);
  and and_6 (and_6_out, and_1_out, DREqI0);
  and and_7 (and_7_out, rB4, not_1_out);
  and and_8 (and_8_out, rB3, AC_0_15[15]);
  and and_9 (and_9_out, rB2, ACEql0);
  and and_10 (and_10_out, D4, T4);
  and and_11 (and_11_out, D5, T5);
  or or_2 (or_2_out, D0, D1, D2, D6);
  and and_12 (INC_DR, D6, T5);
  or or_3 (W_En, and_2_out, and_3_out, and_4_out);
  and and_13 (LD_DR, or_2_out, T4);
  and and_14 (and_14_out, not_2_out, rB1);
  or or_4 (LD_PC, and_10_out, and_11_out);
  // Probe on AL_S2S1S0
  or or_5 (INC_PC, LD_IR, and_6_out, and_7_out, and_8_out, and_9_out, and_14_out);
  not not_2 (not_2_out, E_ff_op);
  and and_15 (out_18, B5, r);
  or or_6 (or_6_out, B6, B7, B9);
  or or_7 (or_7_out, D0, D1, D2);
  and and_16 (and_16_out, D2, T4);
  and and_17 (and_17_out, B11, r);
  not not_3 (not_3_out, out_21);
  or or_8 (or_8_out, D0, D1, D2, D5);
  or or_9 (or_9_out, D3, D4);
  not not_4 (not_4_out, I_output);
  and and_18 (and_18_out, not_3_out, seq_inr);
  and and_19 (and_19_out, or_6_out, r);
  and and_20 (and_20_out, or_7_out, T5);
  or or_10 (or_10_out, in_2, and_18_out);
  or or_11 (out_19, and_19_out, and_20_out);
  or or_12 (out_20, and_16_out, and_17_out);
  and and_21 (and_21_out, T6, D6);
  and and_22 (and_22_out, T5, or_8_out);
  and and_23 (and_23_out, T4, or_9_out);
  and and_24 (and_24_out, T3, not_4_out, D7);
  D_Flip_Flop d_ff_1 (.D(or_10_out), .clk(Clk), .Q(seq_inr));  // open: Qn, preset, reset
  or or_13 (out_21, and_21_out, and_22_out, and_23_out, and_24_out, and_25_out);
  and and_25 (and_25_out, and_24_out, B0);
  // Probe on DR_0_15
  // Probe on common_bus_1_pc_output
  // Probe on common_bus_1_ar_0_15
  common_bus common_bus_1 (
    .Write(W_En), .en(En_rd), .Clk(Clk), .Incr_ar(out_16), .Load_ar(out_17), .Clr_ar(1'b0), .Incr_pc(INC_PC),
    .Load_pc(LD_PC), .S2S1S0({S2, S1, S0}), .Clr_pc(1'b0), .Incr_dr(INC_DR), .Load_dr(LD_DR), .Clr_dr(1'b0),
    .Incr_accu(out_18), .load_ac(out_19), .Clr_accu(out_20), .ALUselect(AL_S2S1S0), .Incr_ir(1'b0),
    .Load_ir(LD_IR), .Clr_ir(1'b0), .Incr_tr(1'b0), .Load_tr(1'b0), .Clr_tr(1'b0), .ComE(E_COMP),
    .Load(LOAD), .Clr(CLR), .ar_0_15(common_bus_1_ar_0_15), .pc_output(common_bus_1_pc_output),
    .dr_0_15(DR_0_15), .ac_0_15(AC_0_15), .ir_0_15(common_bus_1_ir_0_15));  // open: E_ff_op
  Clock clock_1 (.out(Clk));
  // Probe on AC_0_15
  // Probe on AC_0_15
  // Probe on common_bus_1_ir_0_15
  control_unit_o control_unit_o_1 (
    .IR_0_15(common_bus_1_ir_0_15), .seq_clk(Clk), .seq_inr(seq_inr), .seq_clr(out_21),
    .CU_B_output({B11, B10, B9, B8, B7, B6, B5, B4, B3, B2, B1, B0}), .I_output(I_output), .D0(D0), .D1(D1),
    .D2(D2), .D3(D3), .D4(D4), .D5(D5), .D6(D6), .D7(D7),
    .seq_output({T15, T14, T13, T12, T11, T10, T9, T8, T7, T6, T5, T4, T3, T2, LD_IR, T0}));
  or or_14 (or_14_out, AC_0_15[0], AC_0_15[1], AC_0_15[2], AC_0_15[3], AC_0_15[4], AC_0_15[5], AC_0_15[6], AC_0_15[7], AC_0_15[8], AC_0_15[9], AC_0_15[10], AC_0_15[11], AC_0_15[12], AC_0_15[13], AC_0_15[14], AC_0_15[15]);
  or or_15 (or_15_out, DR_0_15[0], DR_0_15[1], DR_0_15[2], DR_0_15[3], DR_0_15[4], DR_0_15[5], DR_0_15[6], DR_0_15[7], DR_0_15[8], DR_0_15[9], DR_0_15[10], DR_0_15[11], DR_0_15[12], DR_0_15[13], DR_0_15[14], DR_0_15[15]);
  not not_5 (DREqI0, or_15_out);
  not not_6 (ACEql0, or_14_out);
  or or_16 (or_16_out, D0, D1, D2, D6);
  not not_7 (not_7_out, I_output);
  and and_26 (Y, or_16_out, T4);
  and and_27 (r, D7, not_7_out, T3);
  and and_28 (rB11, r, B11);
  and and_29 (rB10, r, B10);
  and and_30 (rB9, r, B9);
  and and_31 (rB8, r, B8);
  and and_32 (rB7, r, B7);
  and and_33 (rB6, r, B6);
  and and_34 (rB5, r, B5);
  and and_35 (rB4, r, B4);
  and and_36 (rB3, r, B3);
  and and_37 (rB2, r, B2);
  and and_38 (rB1, r, B1);
  and and_39 (rB0, r, B0);
  or or_17 (rdEN, LD_IR, r, Y);
  and and_40 (and_40_out, D4, T4);
  and and_41 (and_41_out, D5, T5);
  and and_42 (and_42_out, D5, T4);
  and and_43 (and_43_out, D0, T5);
  and and_44 (and_44_out, D1, T5);
  and and_45 (and_45_out, D2, T5);
  and and_46 (and_46_out, D6, T6);
  and and_47 (and_47_out, D0, T5);
  and and_48 (and_48_out, D1, T5);
  and and_49 (and_49_out, D3, T4);
  or or_18 (X5, T2, 1'b0);
  not not_8 (not_8_out, D7);
  or or_19 (or_19_out, D0, D1, D2, D6);
  and and_50 (and_50_out, not_8_out, I_output, T3);
  or or_20 (X1, and_40_out, and_41_out);
  or or_21 (X2, T0, and_42_out);
  or or_22 (X3, and_43_out, and_44_out, and_45_out, and_46_out);
  or or_23 (X4, and_47_out, and_48_out, and_49_out);
  and and_51 (and_51_out, or_19_out, T4);
  or or_24 (En_rd, and_51_out, LD_IR, and_50_out);
  and and_52 (a4, B6, r);
  and and_53 (a5, r, B7);
  and and_54 (a1, D1, T5);
  and and_55 (a2, D0, T5);
  and and_56 (a3, r, B9);
  and and_57 (a0, D2, T5);
  or or_25 (S0, X1, En_rd, X3, X5);
  or or_26 (S1, X3, En_rd, X2, 1'b0);
  or or_27 (S2, X5, X4, 1'b0, En_rd);
  Priority_Encoder priority_encoder_1 (
    .in0(a0), .in1(a1), .in2(a2), .in3(a3), .in4(a4), .in5(a5), .in6(in_1), .in7(in_1), .out(AL_S2S1S0));  // open: en_in, gs, en_out
  // Probe on {S2, S1, S0}
  // Probe on AL_S2S1S0

  // Other names for the same wires on the sheet: T1 = LD_IR; a6 = in_1; a7 = in_1; AC_15 = AC_0_15[15];
  //   CLR_AC = out_20; INC_AC = out_18; INC_AR = out_16; LD_AC = out_19; LD_AR = out_17; S2S1S0[2:0] = {S2, S1, S0};
  //   seq_clr = out_21; X7 = En_rd

  // Notes on the sheet:
  //   memory write enable generation
  //   start stop generation
  //   Memory read Enable generation
endmodule

module garbage (
  input  RST
);

  wire a1, a2, a3, a4, a5, ADD, and_1_out, and_4_out, and_5_out, and_8_out, ANDop, ARload, b0, b1, b2, B5,
       B11, BSA, BUN, D0, D1, D2, D3, D4, D5, D6, D7, E_clr, I_output, Load_ac, Load_ar, Load_dr, Load_ir,
       Memory_read_en, Memory_write_en, n, not_1_out, not_2_out, or_1_out, or_2_out, or_4_out, or_9_out, p,
       PCclr, r, rB6, rB7, rB10, Seq_Clr, STA, T0, T2, T3, T4, T5, undriven, undriven_2, W, Y, Z;

  not not_1 (not_1_out, D7);
  or or_1 (or_1_out, D0, D1, D2);
  or or_2 (or_2_out, D0, D1, D2);
  and and_1 (and_1_out, I_output, not_1_out, T3);
  or or_3 (Load_ar, T0, T2, and_1_out);
  and and_2 (Load_dr, or_1_out, T4);
  and and_3 (Load_ac, or_2_out, T5);
  not not_2 (not_2_out, D7);
  or or_4 (or_4_out, D0, D1, D2);
  and and_4 (and_4_out, or_4_out, T4);
  and and_5 (and_5_out, not_2_out, I_output, T3);
  or or_5 (Memory_read_en, and_4_out, and_5_out, Load_ir);
  and and_6 (Memory_write_en, D3, T4);
  and and_7 (p, D6, I_output, T3);
  buf or_6 (E_clr, rB10);  // OR_Gate
  or or_7 (ARload, T0, undriven, undriven_2);
  buf or_8 (PCclr, RST);  // OR_Gate
  or or_9 (or_9_out, D0, D1, D2);
  and and_8 (and_8_out, T5, or_9_out);
  // OR_Gate or_10 has open pins: in0=and_8_out, in1=a1, in2=a2, in3=a3, in4=a4, in5=a5, out=open
  or or_11 (Seq_Clr, BUN, BUN, ANDop, r, ADD, STA, p, W);
  // AND_Gate and_9 has open pins: in0=r, in1=B11, out=open
  // AND_Gate and_10 has open pins: in0=r, in1=B5, out=open
  or or_12 (b0, a1, a3, a5);
  or or_13 (b1, a3, a2);
  or or_14 (b2, a5, a4);
  and and_11 (BUN, T4, D4);
  and and_12 (BSA, T5, D5);
  // Probe on {b2, b1, b0}
  // OR_Gate or_15 has open pins: in0=BUN, in1=BSA, out=open
  // OR_Gate or_16 has open pins: in2=n, out=open
  // OR_Gate or_17 has open pins: in0=Load_ir, in1=Z, in2=Y, out=open
  and and_13 (ADD, D1, T5);
  and and_14 (ANDop, D0, T5);
  and and_15 (ANDop, D2, T5);
  // OR_Gate or_18 has open pins: in0=T2, out=open
  // OR_Gate or_19 has open pins: in0=STA, out=open
  // OR_Gate or_20 has open pins: in0=ANDop, in3=W, out=open
  // OR_Gate or_21 has open pins: in0=ADD, in1=rB7, in2=rB6, in3=ANDop, out=open

  // Other names for the same wires on the sheet: DR = ANDop; rB9 = ADD; T1 = Load_ir; X1 = Memory_read_en; X2 = T0
endmodule

module ArithmeticLogicalUnit (
  input  [15:0] AC,
  input  [15:0] DR,
  input  IPLS,
  input  IPRS,
  input  [2:0] ALUselect,
  output [15:0] ALUout,
  output Cout
);

  wire [15:0] adder_1_out, and_1_out, not_1_out;

  assign not_1_out = ~AC;  // NOT_Gate not_1, 16 bits wide
  Adder #(.width(16)) adder_1 (.a(AC), .b(DR), .out(adder_1_out), .cin(1'b0), .cout(Cout));
  assign and_1_out = AC & DR;  // AND_Gate and_1, 16 bits wide
  Multiplexer #(.select(3), .width(16)) multiplexer_1 (
    .in0(DR), .in1(adder_1_out), .in2(and_1_out), .in3(not_1_out), .in4({AC[14:0], IPLS}),
    .in5({IPRS, AC[15:1]}), .out(ALUout), .sel(ALUselect));  // open: in6, in7
endmodule
